// Logisim project VHDL_1.circ as structural Verilog: 5 circuits, main circuit Task1_Logic
module Task1_Logic (
  input  a,
  input  b,
  input  c,
  input  d,
  output out1,
  output out2
);

  and AND4 (out1, a, b, c, d);
  or OR4 (out2, a, b, c, d);
endmodule

module Task2_MUX8_1 (
  input  a,
  input  b,
  input  c,
  input  d,
  input  e,
  input  f,
  input  g,
  input  [2:0] ch,
  input  h,
  output data
);

  Multiplexer #(.select(3)) multiplexer_1 (
    .in0(a), .in1(b), .in2(c), .in3(d), .in4(e), .in5(f), .in6(g), .in7(h), .out(data), .sel(ch));
endmodule

module Task3_LED_Letters (
  input  en,
  input  [3:0] dat,
  output [7:0] display
);

  ROM #(.addrWidth(4), .dataWidth(8)) rom_1 (.addr(dat));  // open: data
  _7_Segment_Display u_7_segment_display_1 ();  // open: g, f, a, b, e, d, c, dp

  // Notes on the sheet:
  //   contents of rom_1 (hex, n*v repeats v):
  //   ee 3e 9c 7a 8e f6 f6 0 0 0 ee 3e 9c 7a 0 8e
endmodule

module Task4_Vote25 (
  input  [24:0] vt,
  output result
);

  wire comparator_1_eq, comparator_1_gt;
  wire [4:0] bitadder_1_out;

  BitAdder #(.width(25)) bitadder_1 (.in0(vt), .out(bitadder_1_out));
  Comparator #(.mode("unsigned"), .width(5)) comparator_1 (
    .a(bitadder_1_out), .b(5'b01101), .gt(comparator_1_gt), .eq(comparator_1_eq));  // open: lt
  // OR_Gate or_1 has open pins: out=result
endmodule

module Task5_Vote13_LED (
  input  en,
  input  [12:0] vt,
  output [7:0] display
);

  wire [3:0] bitadder_1_out;
  wire [7:0] undriven;

  BitAdder #(.width(13)) bitadder_1 (.in0(vt), .out(bitadder_1_out));
  ROM #(.addrWidth(4), .dataWidth(8)) rom_1 (.addr(bitadder_1_out));  // open: data
  Multiplexer #(.width(8)) multiplexer_1 (.in0({8{1'b0}}), .in1(undriven), .out(display), .sel(en));

  // Notes on the sheet:
  //   contents of rom_1 (hex, n*v repeats v):
  //   fc 60 da f2 66 b6 be e0 fe f6 ee 3e 9c 7a 9e 8e
endmodule
